# Fritzing sketch Project (saved by Fritzing 0.9.3b)
breadboards: 1

parts:
  U1 = ESP8266 WiFi Module [part_number=ESP8266]
  Componente1 = Arduino Uno (Rev3)
  Part1 = KY-018 Photoresistor Module [package="Breakout board"]
  DHT1 = DHT11 Humitidy and Temperature Sensor
  Componente2 = FC-28 Soil Hygrometer Module
  YL-83_-_Detection_Board1 = YL-83 Rain Sensor - Detection Board

nets:
  N1: U1.RXD, Componente1.D0/RX
  VCC: U1.VCC, U1.CH_PD, Componente1.3V3
  N2: U1.GPIO_0, Componente1.D3_PWM
  GND: U1.GND, Componente1.GND, Part1.-, DHT1.GND, Componente2.GND
  N3: U1.TXD, Componente1.D1/TX
  N4: Componente1.A0, Componente2.AO
  N5: Componente1.A2, Part1.S
  N6: Componente1.D12/MISO, Componente2.DO
  N7: Componente1.D13/SCK, DHT1.DATA
  5V: Componente1.5V, Part1.Vin, DHT1.VDD, Componente2.VCC
  N8: Componente2.POS, YL-83_-_Detection_Board1.POS
  N9: Componente2.NEG, YL-83_-_Detection_Board1.NEG

custom parts:
  ESP8266 WiFi Module: Generic WiFi Module based on the ESP8266 with onboard PCB antenna and UART communications
  KY-018 Photoresistor Module: KY-018 Photoresistor module, used to measure light intensity. It can determine the presence or absence of light.
  DHT11 Humitidy and Temperature Sensor: DHT11 Humidity and Temperature Sensor
  FC-28 Soil Hygrometer Module: The FC-28 is a soil hygrometer module that uses the Texas Instruments LM393 comparator chip to provide an analog measurement of soil humidity. The digital output is high when soil moisture is over a certain threshold, as determined by adjusting the potentiometer.
  YL-83 Rain Sensor - Detection Board: The YL-83 is a rain sensor that has more resistance when dry and less resistance when wet. The module runs at 5V.
